# Fritzing sketch TriMetricSerial (saved by Fritzing 0.9.3b)
breadboards: 1

parts:
  part = Voltage Regulator - 5V [package="TO220 [THT]"]
  part_2 = Arduino Uno (Rev3) - ICSP
  TM2030_J2 = RJ11 Jack [package=rj11-6]
  D1_1N4148 = Diode [package=diode-1n4148]
  D2_1N4148 = Diode [package=diode-1n4148]
  R1 = Resistor [tolerance=±5% resistance=47k package="0402 [SMD]"]
  R2 = Resistor [tolerance=±5% resistance=47k package="0402 [SMD]"]
  V1_-_From_TM2030_B1_&_G1 = DC Power [voltage=12V]

nets:
  N1: part.input_voltage, V1_-_From_TM2030_B1_&_G1.V+
  GND: part.GND, part_2.GND, V1_-_From_TM2030_B1_&_G1.V-
  N2: part.output_voltage, part_2.5V, R1.Pin_0, R2.Pin_0
  N3: part_2.D2, D1_1N4148.A, R2.Pin_1
  N4: part_2.D4, D2_1N4148.A, R1.Pin_1
  N5: TM2030_J2.2, D1_1N4148.C
  N6: TM2030_J2.3, D2_1N4148.C

notes:
  12V
  (from TM2030 B1 & G1)
  COM-00107
